# Fritzing sketch AR17_dm_module (saved by Fritzing 0.9.3b)

parts:
  부품1 = Arduino Uno (Rev3)
  8x8_LED_Modul_mit_MAX1 = 8x8 LED Modul mit MAX7219 [package=THT]

nets:
  N1: 부품1.5V, 8x8_LED_Modul_mit_MAX1.VCC_Eingang
  N2: 부품1.GND, 8x8_LED_Modul_mit_MAX1.GND_Eingang
